# Fritzing sketch KeypadRFID (saved by Fritzing 0.9.3b)

parts:
  Part1 = Arduino Uno (Rev3)
  Part2 = RFID-RC522-v3
  Matrix_keypad1 = KEYPAD 4x4

nets:
  N1: Part1.D8, Matrix_keypad1.row1
  N2: Part1.D9_PWM, Part2.RST
  N3: Part1.D10_PWM/SS, Part2.SDA
  N4: Part1.D11_PWM/MOSI, Part2.MOSI
  N5: Part1.D12/MISO, Part2.MISO
  N6: Part1.D13/SCK, Part2.SCK
  GND: Part1.GND, Part2.GND
  N7: Part1.D0/RX, Matrix_keypad1.col4
  N8: Part1.D2, Matrix_keypad1.col3
  N9: Part1.D3_PWM, Matrix_keypad1.col2
  N10: Part1.D4, Matrix_keypad1.col1
  N11: Part1.D5_PWM, Matrix_keypad1.row4
  N12: Part1.D6_PWM, Matrix_keypad1.row3
  N13: Part1.D7, Matrix_keypad1.row2
  3V3: Part1.3V3, Part2.3.3V

custom parts:
  RFID-RC522-v3: A simple China made RFID-RC522 Reader (6x4 cm); do check the pin labels, as this is a MFRC522 based clone.
  KEYPAD 4x4: Matrix keypad 16 buttons, 4 rows x 4 columns
